// Logisim project Practica03.circ as structural Verilog: 3 circuits, main circuit Ejercicio1
module Ejercicio1 (
  input  x1,
  input  x2,
  output out_3
);

  Transistor transistor_1 (.in(1'b1), .out(out_3), .gate(x1));
  Transistor #(.\type ("n")) transistor_2 (.in(1'b1), .out(out_3), .gate(x2));
  Transistor #(.\type ("n")) transistor_3 (.in(x2), .out(out_3), .gate(x1));
endmodule

module Ejercicio2_1 (
  input  x1,
  input  x2,
  input  y1,
  input  y2,
  output M
);

  wire and_1_out, and_2_out, and_3_out, not_1_out, not_2_out;

  not not_1 (not_1_out, x1);
  not not_2 (not_2_out, x2);
  and and_1 (and_1_out, not_1_out, y2, not_2_out);
  and and_2 (and_2_out, not_2_out, y1, y2);
  and and_3 (and_3_out, not_1_out, y1);
  or or_1 (M, and_1_out, and_2_out, and_3_out);
endmodule

module Ejercicio2_2 (
  input  x1,
  input  x2,
  input  y1,
  input  y2,
  output out_5
);

  wire and_1_out, and_2_out, and_3_out, and_4_out, not_1_out, not_2_out, not_3_out, not_4_out;

  not not_1 (not_1_out, x1);
  not not_2 (not_2_out, x2);
  not not_3 (not_3_out, y1);
  not not_4 (not_4_out, y2);
  and and_1 (and_1_out, not_1_out, not_2_out, not_3_out, not_4_out);
  and and_2 (and_2_out, not_1_out, x2, not_3_out, y2);
  and and_3 (and_3_out, x1, not_2_out, y1, not_4_out);
  and and_4 (and_4_out, x1, x2, y1);
  or or_1 (out_5, and_1_out, and_2_out, and_3_out, and_4_out);
endmodule
