// Logisim project Practica04.circ as structural Verilog: 5 circuits, main circuit Full Adder 1 bit
module Full_Adder_1_bit (
  input  A,
  input  B,
  input  C_i,
  output Sum,
  output C_i_1
);

  wire and_1_out, and_2_out, xor_1_out;

  and and_1 (and_1_out, B, A);
  xor xor_1 (xor_1_out, A, B);
  and and_2 (and_2_out, C_i, xor_1_out);
  or or_1 (C_i_1, and_2_out, and_1_out);
  xor xor_2 (Sum, xor_1_out, C_i);
endmodule

module Adder_8_bits (
  input  [7:0] A,
  input  [7:0] B,
  output [7:0] Suma,
  output Desborde
);

  wire full_adder_1_bit_2_c_i_1, full_adder_1_bit_3_c_i_1, full_adder_1_bit_4_c_i_1,
       full_adder_1_bit_5_c_i_1, full_adder_1_bit_6_c_i_1, full_adder_1_bit_7_c_i_1, full_adder_1_bit_8_c_i_1;

  Full_Adder_1_bit full_adder_1_bit_1 (
    .A(A[7]), .B(B[7]), .C_i(full_adder_1_bit_2_c_i_1), .Sum(Suma[7]), .C_i_1(Desborde));
  Full_Adder_1_bit full_adder_1_bit_2 (
    .A(A[6]), .B(B[6]), .C_i(full_adder_1_bit_3_c_i_1), .Sum(Suma[6]), .C_i_1(full_adder_1_bit_2_c_i_1));
  Full_Adder_1_bit full_adder_1_bit_3 (
    .A(A[5]), .B(B[5]), .C_i(full_adder_1_bit_4_c_i_1), .Sum(Suma[5]), .C_i_1(full_adder_1_bit_3_c_i_1));
  Full_Adder_1_bit full_adder_1_bit_4 (
    .A(A[4]), .B(B[4]), .C_i(full_adder_1_bit_5_c_i_1), .Sum(Suma[4]), .C_i_1(full_adder_1_bit_4_c_i_1));
  Full_Adder_1_bit full_adder_1_bit_5 (
    .A(A[3]), .B(B[3]), .C_i(full_adder_1_bit_6_c_i_1), .Sum(Suma[3]), .C_i_1(full_adder_1_bit_5_c_i_1));
  Full_Adder_1_bit full_adder_1_bit_6 (
    .A(A[2]), .B(B[2]), .C_i(full_adder_1_bit_7_c_i_1), .Sum(Suma[2]), .C_i_1(full_adder_1_bit_6_c_i_1));
  Full_Adder_1_bit full_adder_1_bit_7 (
    .A(A[1]), .B(B[1]), .C_i(full_adder_1_bit_8_c_i_1), .Sum(Suma[1]), .C_i_1(full_adder_1_bit_7_c_i_1));
  Full_Adder_1_bit full_adder_1_bit_8 (.A(A[0]), .B(B[0]), .C_i(1'b0), .Sum(Suma[0]), .C_i_1(full_adder_1_bit_8_c_i_1));

  // Notes on the sheet:
  //   Sum7
  //   A
  //   C7
  //   Sum6
  //   C6
  //   Sum5
  //   C5
  //   Sum4
  //   Salida
  //   C4
  //   Sum3
  //   C3
  //   Sum2
  //   B
  //   C2
  //   Sum1
  //   Sum0
  //   C1
endmodule

module Compleamento_A2 (
  input  [7:0] A,
  output [7:0] not_A
);

  wire [7:0] not_1_out;

  not not_1 (not_1_out[0], A[0]);
  not not_2 (not_1_out[1], A[1]);
  not not_3 (not_1_out[2], A[2]);
  not not_4 (not_1_out[3], A[3]);
  not not_5 (not_1_out[4], A[4]);
  not not_6 (not_1_out[5], A[5]);
  not not_7 (not_1_out[6], A[6]);
  not not_8 (not_1_out[7], A[7]);
  Adder_8_bits adder_8_bits_1 (.A(not_1_out), .B(8'h1), .Suma(not_A));  // open: Desborde
endmodule

module Restador_Sumador (
  input  [7:0] A,
  input  [7:0] B,
  input  Opcion,
  output [7:0] Salida
);

  wire [7:0] compleamento_a2_1_not_a, multiplexer_1_out;

  Compleamento_A2 compleamento_a2_1 (.A(B), .not_A(compleamento_a2_1_not_a));
  Multiplexer #(.width(8), .enable("false")) multiplexer_1 (
    .in0(B), .in1(compleamento_a2_1_not_a), .out(multiplexer_1_out), .sel(Opcion));
  Adder_8_bits adder_8_bits_1 (.A(A), .B(multiplexer_1_out), .Suma(Salida));  // open: Desborde
endmodule

module Simulador (
  input  [7:0] A,
  input  [7:0] B,
  input  Opcion,
  output [7:0] Salida
);

  Restador_Sumador restador_sumador_1 (.A(A), .B(B), .Opcion(Opcion), .Salida(Salida));
endmodule
