// Logisim project practica04.circ as structural Verilog: 5 circuits, main circuit Sumador 1-Bit
module Sumador_1_Bit (
  input  C_in,
  input  A,
  input  B,
  output S,
  output C_out
);

  wire and_1_out, and_2_out, and_3_out, and_4_out, and_5_out, and_6_out, and_7_out, not_1_out, not_2_out,
       not_3_out;

  not not_1 (not_1_out, A);
  not not_2 (not_2_out, B);
  not not_3 (not_3_out, C_in);
  and and_1 (and_1_out, C_in, not_1_out, not_2_out);
  and and_2 (and_2_out, not_3_out, not_1_out, B);
  and and_3 (and_3_out, C_in, B, A);
  and and_4 (and_4_out, not_3_out, not_2_out, A);
  and and_5 (and_5_out, B, A);
  and and_6 (and_6_out, C_in, B);
  and and_7 (and_7_out, C_in, A);
  or or_1 (S, and_1_out, and_2_out, and_3_out, and_4_out);
  or or_2 (C_out, and_5_out, and_6_out, and_7_out);
endmodule

module Sumador_8_Bits (
  input  [7:0] A,
  input  [7:0] B,
  output [7:0] A___B,
  output Desbordamiento
);

  wire sumador_1_bit_1_c_out, sumador_1_bit_2_c_out, sumador_1_bit_3_c_out, sumador_1_bit_4_c_out,
       sumador_1_bit_5_c_out, sumador_1_bit_6_c_out, sumador_1_bit_7_c_out;

  Sumador_1_Bit sumador_1_bit_1 (.A(A[0]), .B(B[0]), .C_in(1'b0), .C_out(sumador_1_bit_1_c_out), .S(A___B[0]));
  Sumador_1_Bit sumador_1_bit_2 (
    .A(A[1]), .B(B[1]), .C_in(sumador_1_bit_1_c_out), .C_out(sumador_1_bit_2_c_out), .S(A___B[1]));
  Sumador_1_Bit sumador_1_bit_3 (
    .A(A[2]), .B(B[2]), .C_in(sumador_1_bit_2_c_out), .C_out(sumador_1_bit_3_c_out), .S(A___B[2]));
  Sumador_1_Bit sumador_1_bit_4 (
    .A(A[3]), .B(B[3]), .C_in(sumador_1_bit_3_c_out), .C_out(sumador_1_bit_4_c_out), .S(A___B[3]));
  Sumador_1_Bit sumador_1_bit_5 (
    .A(A[4]), .B(B[4]), .C_in(sumador_1_bit_4_c_out), .C_out(sumador_1_bit_5_c_out), .S(A___B[4]));
  Sumador_1_Bit sumador_1_bit_6 (
    .A(A[5]), .B(B[5]), .C_in(sumador_1_bit_5_c_out), .C_out(sumador_1_bit_6_c_out), .S(A___B[5]));
  Sumador_1_Bit sumador_1_bit_7 (
    .A(A[6]), .B(B[6]), .C_in(sumador_1_bit_6_c_out), .C_out(sumador_1_bit_7_c_out), .S(A___B[6]));
  Sumador_1_Bit sumador_1_bit_8 (
    .A(A[7]), .B(B[7]), .C_in(sumador_1_bit_7_c_out), .C_out(Desbordamiento), .S(A___B[7]));
endmodule

module Inverso_Comp__a_2 (
  input  [7:0] A,
  output [7:0] A_2
);

  wire [7:0] not_1_out;

  not not_1 (not_1_out[0], A[0]);
  not not_2 (not_1_out[1], A[1]);
  not not_3 (not_1_out[2], A[2]);
  not not_4 (not_1_out[3], A[3]);
  not not_5 (not_1_out[4], A[4]);
  not not_6 (not_1_out[5], A[5]);
  not not_7 (not_1_out[6], A[6]);
  not not_8 (not_1_out[7], A[7]);
  Sumador_8_Bits sumador_8_bits_1 (.A(not_1_out), .B(8'h1), .A___B(A_2));  // open: Desbordamiento
endmodule

module Sumador_y_Restador_8_Bits (
  input  in_1,
  input  [7:0] A,
  input  [7:0] B,
  output [7:0] A___B___A___B,
  output Desbordamiento
);

  wire [7:0] inverso_comp_a_2_1_a_2, multiplexer_1_out;

  Inverso_Comp__a_2 inverso_comp_a_2_1 (.A(B), .A_2(inverso_comp_a_2_1_a_2));
  Multiplexer #(.width(8), .enable("false")) multiplexer_1 (
    .in0(B), .in1(inverso_comp_a_2_1_a_2), .out(multiplexer_1_out), .sel(in_1));
  Sumador_8_Bits sumador_8_bits_1 (
    .A(A), .B(multiplexer_1_out), .Desbordamiento(Desbordamiento), .A___B(A___B___A___B));
endmodule

module Sumador_Restador_final (
  input  Operador,
  input  [7:0] A,
  input  [7:0] B,
  output [7:0] Resultado,
  output Desbordamiento
);

  Sumador_y_Restador_8_Bits sumador_y_restador_8_bits_1 (
    .A(A), .B(B), .in_1(Operador), .A___B___A___B(Resultado), .Desbordamiento(Desbordamiento));
endmodule
