// Logisim project practica05.circ as structural Verilog: 5 circuits, main circuit Banco de Registros
module \Autómata  (
  input  In,
  output A,
  output B
);

  wire and_1_out, clock_1_out, not_1_out;

  not not_1 (not_1_out, In);
  and and_1 (and_1_out, not_1_out, B);
  Clock clock_1 (.out(clock_1_out));
  J_K_Flip_Flop u_A (.J(and_1_out), .clk(clock_1_out), .K(and_1_out), .Q(A));  // open: Qn, preset, en, reset
  J_K_Flip_Flop u_B (.J(not_1_out), .clk(clock_1_out), .K(B), .Q(B));  // open: Qn, preset, en, reset

  // Notes on the sheet:
  //   A: pull=up
  //   B: pull=up
endmodule

module Registro (
  input  [7:0] Entrada,
  input  \Opción ,
  output [7:0] Salida__Guardada
);

  D_Flip_Flop d_ff_1 (.clk(\Opción ), .D(Entrada[0]), .Q(Salida__Guardada[0]));  // open: Qn, preset, en, reset
  D_Flip_Flop d_ff_2 (.clk(\Opción ), .D(Entrada[1]), .Q(Salida__Guardada[1]));  // open: Qn, preset, en, reset
  D_Flip_Flop d_ff_3 (.clk(\Opción ), .D(Entrada[2]), .Q(Salida__Guardada[2]));  // open: Qn, preset, en, reset
  D_Flip_Flop d_ff_4 (.clk(\Opción ), .D(Entrada[3]), .Q(Salida__Guardada[3]));  // open: Qn, preset, en, reset
  D_Flip_Flop d_ff_5 (.clk(\Opción ), .D(Entrada[4]), .Q(Salida__Guardada[4]));  // open: Qn, preset, en, reset
  D_Flip_Flop d_ff_6 (.clk(\Opción ), .D(Entrada[5]), .Q(Salida__Guardada[5]));  // open: Qn, preset, en, reset
  D_Flip_Flop d_ff_7 (.clk(\Opción ), .D(Entrada[6]), .Q(Salida__Guardada[6]));  // open: Qn, preset, en, reset
  D_Flip_Flop d_ff_8 (.clk(\Opción ), .D(Entrada[7]), .Q(Salida__Guardada[7]));  // open: Qn, preset, en, reset
endmodule

module Selector_Escribir (
  input  in_1,
  input  [1:0] in_2,
  output [3:0] out_3
);

  wire decoder_1_out0, decoder_1_out1, decoder_1_out2, decoder_1_out3;

  Decoder #(.select(2), .enable("false")) decoder_1 (
    .out0(decoder_1_out0), .out1(decoder_1_out1), .out2(decoder_1_out2), .out3(decoder_1_out3), .sel(in_2));
  and and_1 (out_3[0], decoder_1_out0, in_1);
  and and_2 (out_3[1], decoder_1_out1, in_1);
  and and_3 (out_3[3], decoder_1_out2, in_1);
  and and_4 (out_3[3], decoder_1_out3, in_1);

  assign out_3[2] = out_3[3];
endmodule

module Banco_de_Registros (
  input  [1:0] Registro_1,
  input  [1:0] Registro_2,
  input  [1:0] Escribir_Registro,
  input  [7:0] Escribir_Datos,
  input  \Opción ,
  output [7:0] Datos_1,
  output [7:0] Datos_2
);

  wire [3:0] selector_escribir_1_out_3;
  wire [7:0] registro_1_salida__guardada, registro_2_salida__guardada, registro_3_salida__guardada,
       registro_4_salida__guardada;

  Selector_Escribir selector_escribir_1 (.in_2(Escribir_Registro), .out_3(selector_escribir_1_out_3));  // open: in_1
  Registro u_registro_1 (.Entrada(Escribir_Datos), .Salida__Guardada(registro_1_salida__guardada));  // open: Opción
  Registro u_registro_2 (.Entrada(Escribir_Datos), .Salida__Guardada(registro_2_salida__guardada));  // open: Opción
  Registro registro_3 (.Entrada(Escribir_Datos), .Salida__Guardada(registro_3_salida__guardada));  // open: Opción
  Registro registro_4 (.Entrada(Escribir_Datos), .Salida__Guardada(registro_4_salida__guardada));  // open: Opción
  Multiplexer #(.select(2), .width(8), .enable("false")) multiplexer_1 (
    .in0(registro_1_salida__guardada), .in1(registro_2_salida__guardada), .in2(registro_3_salida__guardada),
    .in3(registro_4_salida__guardada), .out(Datos_1), .sel(Registro_1));
  Multiplexer #(.select(2), .width(8), .enable("false")) multiplexer_2 (
    .in0(registro_1_salida__guardada), .in1(registro_2_salida__guardada), .in2(registro_3_salida__guardada),
    .in3(registro_4_salida__guardada), .out(Datos_2), .sel(Registro_2));
endmodule

module Sumador (
  input  [15:0] in_1
);

  wire clock_1_out;
  wire [7:0] banco_de_registros_1_datos_1, banco_de_registros_1_datos_2, multiplexer_1_out,
       sumador_restador_final_1_resultado;

  Clock clock_1 (.out(clock_1_out));
  Banco_de_Registros banco_de_registros_1 (
    .Registro_1(in_1[11:10]), .Registro_2(in_1[9:8]), .Escribir_Registro(in_1[13:12]),
    .Escribir_Datos(sumador_restador_final_1_resultado), .\Opción (clock_1_out),
    .Datos_1(banco_de_registros_1_datos_1), .Datos_2(banco_de_registros_1_datos_2));
  Multiplexer #(.width(8), .enable("false")) multiplexer_1 (
    .in0(banco_de_registros_1_datos_2), .in1(in_1[7:0]), .out(multiplexer_1_out), .sel(in_1[14]));
  Sumador_Restador_final sumador_restador_final_1 (
    .A(banco_de_registros_1_datos_1), .B(multiplexer_1_out), .Operador(in_1[15]),
    .Resultado(sumador_restador_final_1_resultado));  // open: Desbordamiento
endmodule
